# Fritzing sketch Fritzing_The_Vibrating_Pressure_Sensor (saved by Fritzing 0.9.3b)
breadboards: 2

parts:
  Part1 = Arduino Nano (Rev3.0) (ICSP)
  Part2 = Barometric Pressure Sensor - BMP180 Breakout (GY-68)
  U1 = Vibration Motor- ROB-08449 [package=vibe-motor-10mm]
  U2 = POT [package=pot_mammoth]
  LCD1 = LCD screen
  LED1 = smd LED [color="Red (633nm)" package="0603 [SMD]"]
  LED2 = smd LED [color="Red (633nm)" package="0603 [SMD]"]
  Part3 = KY-017 Mercury Tilt Switch [package="Breakout board"]
  R1 = Resistor [tolerance=±5% resistance=220 package="2010 [SMD]"]
  R2 = Resistor [tolerance=±5% resistance=220 package="2010 [SMD]"]
  R3 = Resistor [tolerance=±5% resistance=220 package="2010 [SMD]"]

nets:
  GND: Part1.GND, Part2.GND, U1.+, U2.S, LCD1.VSS, LCD1.R/W, LCD1.LED-, R1.Pin_0, R2.Pin_0, R3.Pin_0
  N1: Part1.D2, LCD1.DB7
  N2: Part1.D3, LCD1.DB6
  N3: Part1.D4, LCD1.DB5
  N4: Part1.D5, LCD1.DB4
  N5: Part1.D6, LCD1.E
  N6: Part1.D7, LCD1.RS
  N7: Part1.D8, Part3.-, R1.Pin_1
  N8: Part1.D9, LED1.cathode
  N9: Part1.D10, LED2.cathode
  N10: Part1.D11/MOSI, U1.-
  5V: Part1.5V, Part2.VCC, U2.E, LCD1.VDD, LCD1.LED+, Part3.S
  N11: Part1.A5, Part2.SCL
  N12: Part1.A4, Part2.SDA
  N13: U2.A, LCD1.V0
  N14: LED1.anode, R3.Pin_1
  N15: LED2.anode, R2.Pin_1

notes:
  I used a mercury sensor instead of using a module like this.
  Vibration Motor

custom parts:
  KY-017 Mercury Tilt Switch: Arduino KY-017 mercury tilt switch module, it uses a small mercury ball that completes the circuit when you tilt the module.
